// Digital circuit MIPS32SOC.dig as structural Verilog
module MIPS32SOC (
  input  rst,
  input  clk,
  output invalid_opcode,
  output invalid_addr,
  output invalid_pc
);

  wire aluSrc, and_1_out, and_2_out, branchEqual, branchNotEqual, bsh, isZero, Jump, memRead, memToReg,
       memWrite, not_1_out, RegDst, RegWrite;
  wire [2:0] aluFunc, aluOp;
  wire [4:0] multiplexer_4_out;
  wire [5:0] Func, Opcode;
  wire [7:0] alu_1_res_2;
  wire [27:8] shift_jump;
  wire [31:0] add_1_s, alu_1_res, Data_Mem_d, multiplexer_1_out, multiplexer_2_out, multiplexer_3_out,
       multiplexer_5_out, multiplexer_6_out, PC_plus_4, PC_q, Reg_File_da, Reg_File_db;
  wire [31:2] shift_shift;
  wire [31:30] bitextender_1_out;

  Multiplexer #(.Bits(32)) multiplexer_1 (.sel(bsh), .in_0(PC_plus_4), .in_1(add_1_s), .out(multiplexer_1_out));
  Add #(.Bits(32)) add_1 (.a(PC_plus_4), .b({shift_shift, 2'b00}), .c_i(1'b0), .s(add_1_s));  // open: c_o
  Multiplexer #(.Bits(32)) multiplexer_2 (
    .sel(Jump), .in_0(multiplexer_1_out), .in_1({PC_plus_4[31:28], shift_jump, Func, 2'b00}),
    .out(multiplexer_2_out));
  Multiplexer #(.Bits(32)) multiplexer_3 (
    .sel(rst), .in_0(multiplexer_2_out), .in_1({32{1'b0}}), .out(multiplexer_3_out));
  Register #(.Bits(32)) PC (.D(multiplexer_3_out), .C(clk), .en(1'b1), .Q(PC_q));
  not not_1 (not_1_out, isZero);
  Add #(.Bits(32)) add_2 (.a(PC_q), .b(32'h4), .c_i(1'b0), .s(PC_plus_4));  // open: c_o
  ControlUnit controlunit_1 (
    .Opcode(Opcode), .Reset(rst), .aluSrc(aluSrc), .RegDst(RegDst), .aluOp(aluOp), .memToReg(memToReg),
    .memRead(memRead), .memWrite(memWrite), .RegWrite(RegWrite), .branchNotEqual(branchNotEqual),
    .branchEqual(branchEqual), .Jump(Jump));
  and and_1 (and_1_out, branchEqual, isZero);
  and and_2 (and_2_out, branchNotEqual, not_1_out);
  ROM #(.AddrBits(8), .Bits(32)) InstMem (.A(PC_q[9:2]), .sel(1'b1), .D({Opcode, shift_jump, Func}));
  or or_1 (bsh, and_1_out, and_2_out);
  Multiplexer #(.Bits(5)) multiplexer_4 (
    .sel(RegDst), .in_0(shift_jump[22:18]), .in_1(shift_jump[17:13]), .out(multiplexer_4_out));
  BitExtender #(.inputBits(16), .outputBits(32)) bitextender_1 (
    .in({shift_jump[17:8], Func}), .out({bitextender_1_out, shift_shift}));
  RegisterFile #(.AddrBits(5), .Bits(32)) Reg_File (
    .Din(multiplexer_6_out), .we(RegWrite), .Rw(multiplexer_4_out), .C(clk), .Ra(shift_jump[27:23]),
    .Rb(shift_jump[22:18]), .Da(Reg_File_da), .Db(Reg_File_db));
  Multiplexer #(.Bits(32)) multiplexer_5 (
    .sel(aluSrc), .in_0(Reg_File_db), .in_1({bitextender_1_out, shift_shift}), .out(multiplexer_5_out));
  ALU alu_1 (
    .a(Reg_File_da), .b(multiplexer_5_out), .op(aluFunc),
    .res({alu_1_res[31:10], alu_1_res_2, alu_1_res[1:0]}), .isZero(isZero));  // open: lower, higher
  RAMDualPort #(.AddrBits(8), .Bits(32)) Data_Mem (
    .A(alu_1_res_2), .Din(Reg_File_db), .str(memWrite), .C(clk), .ld(memRead), .D(Data_Mem_d));
  ALUControl alucontrol_1 (.aluOp(aluOp), .Func(Func), .aluFunc(aluFunc));
  Multiplexer #(.Bits(32)) multiplexer_6 (
    .sel(memToReg), .in_0({alu_1_res[31:10], alu_1_res_2, alu_1_res[1:0]}), .in_1(Data_Mem_d),
    .out(multiplexer_6_out));

  assign invalid_addr = 1'b0;
  assign invalid_opcode = 1'b0;
  assign invalid_pc = 1'b0;

  // Other names for the same wires on the sheet: shift_jump (some bits) = {PC_plus_4[31:28], Func}

  // Notes on the sheet:
  //   contents of InstMem (hex, n*v repeats v):
  //   8c080000,8c090004,ac080008
endmodule
